// Digital circuit Circuito.dig as structural Verilog
module Circuito (
  input  Clock,
  input  _1,
  input  [4:0] Selecao_de_Reg_Escalar,
  input  Reset,
  input  [4:0] Selecao_de_Reg_Vetorial,
  output Hazard_Stall,
  output Hazard_Flush,
  output [31:0] Stage_Ex_PC,
  output [31:0] Stage_ID_PC,
  output [31:0] Stage_IF_PC,
  output [31:0] Reg_Debug,
  output [31:0] Alu_Result_Debug,
  output [31:0] Instr_Debug,
  output [31:0] PC_Debug,
  output [31:0] VectorReg_Lane_0,
  output [31:0] VectorReg_Lane_1,
  output [31:0] VectorReg_Lane_2,
  output [31:0] VectorReg_Lane_3,
  output [31:0] VectorAlu_Lane_0,
  output [31:0] VectorAlu_Lane_1,
  output [31:0] Vector_Alu_Lane_2,
  output [31:0] VectorAlu_Lane_3
);

  wire u_riscv_cpu_vector_dmem_we_o;
  wire [31:0] ramdualport_1_d, ROM_d, u_riscv_cpu_vector_dmem_addr_o, u_riscv_cpu_vector_dmem_wdata_o,
       u_riscv_cpu_vector_imem_addr_o;

  riscv_cpu_vector #(.applicationType("GHDL"), .ghdlOptions("--std=08 --ieee=synopsys --workdir=\"C:\\Users\\breno\\OneDrive\\Documentos\\RiscV-Vetorial\""), .CodeFile("C:\\Users\\breno\\OneDrive\\Documentos\\RiscV-Vetorial\\riscv_cpu_vector.vhd")) u_riscv_cpu_vector (
    .clk_i(Clock), .reset_i(Reset), .load_enable_i(Reset), .imem_data_i(ROM_d),
    .dmem_rdata_i(ramdualport_1_d), .reg_sel_i(Selecao_de_Reg_Escalar), .vreg_sel_i(Selecao_de_Reg_Vetorial),
    .imem_addr_o(u_riscv_cpu_vector_imem_addr_o), .dmem_addr_o(u_riscv_cpu_vector_dmem_addr_o),
    .dmem_wdata_o(u_riscv_cpu_vector_dmem_wdata_o), .dmem_we_o(u_riscv_cpu_vector_dmem_we_o),
    .pc_debug_o(PC_Debug), .instr_debug_o(Instr_Debug), .alu_result_debug_o(Alu_Result_Debug),
    .reg_debug_o(Reg_Debug), .stage_if_pc_o(Stage_IF_PC), .stage_id_pc_o(Stage_ID_PC),
    .stage_ex_pc_o(Stage_Ex_PC), .hazard_stall_o(Hazard_Stall), .hazard_flush_o(Hazard_Flush),
    .vreg_debug_lane0_o(VectorReg_Lane_0), .vreg_debug_lane1_o(VectorReg_Lane_1),
    .vreg_debug_lane2_o(VectorReg_Lane_2), .vreg_debug_lane3_o(VectorReg_Lane_3),
    .valu_result_lane0_o(VectorAlu_Lane_0), .valu_result_lane1_o(VectorAlu_Lane_1),
    .valu_result_lane2_o(Vector_Alu_Lane_2), .valu_result_lane3_o(VectorAlu_Lane_3));
  ROM #(.AddrBits(8), .Bits(32)) ROM (.A(u_riscv_cpu_vector_imem_addr_o[9:2]), .sel(_1), .D(ROM_d));
  RAMDualPort #(.AddrBits(8), .Bits(32)) ramdualport_1 (
    .A(u_riscv_cpu_vector_dmem_addr_o[9:2]), .Din(u_riscv_cpu_vector_dmem_wdata_o),
    .str(u_riscv_cpu_vector_dmem_we_o), .C(Clock), .ld(_1), .D(ramdualport_1_d));

  // Notes on the sheet:
  //   contents of ROM (hex, n*v repeats v):
  //   50208b,30210b,20818b,4020820b,20b28b,13
endmodule
